# Fritzing sketch receiver (saved by Fritzing 0.9.5d)
breadboards: 1

parts:
  M5 = DC Motor
  M6 = DC Motor  # not connected
  LED3 = LED - 5mm [color="Blue (470nm)" package="5 mm [THT]"]
  VCC5 = Battery
  VCC6 = Battery
  Q17 = NPN-Transistor [package="TO92 [THT]"]
  Q18 = PNP-Transistor [package="TO92 [THT]"]
  Компонент5 = Arduino Nano (Rev3.0)
  Q19 = NPN-Transistor [package="TO92 [THT]"]
  Q20 = PNP-Transistor [package="TO92 [THT]"]
  Q21 = NPN-Transistor [package="TO92 [THT]"]
  Q22 = PNP-Transistor [package="TO92 [THT]"]
  Q23 = NPN-Transistor [package="TO92 [THT]"]
  Q24 = PNP-Transistor [package="TO92 [THT]"]
  R3 = Resistor [tolerance=±5% resistance=10000 package=THT]
  Компонент6 = NRF24L01+ Breakout Board

nets:
  N1: M5.pin_1, Q23.C, Q24.C
  N2: M5.pin_2, Q21.C, Q22.C
  N3: LED3.cathode, Компонент5.D2
  N4: LED3.anode, R3.Pin_0
  N5: VCC5.-, Q18.B, Q20.B
  N6: VCC5.+, Q17.B, Q19.B
  N7: VCC6.-, Q22.B, Q24.B
  N8: VCC6.+, Q21.B, Q23.B
  N9: Q17.E, Q18.E, Компонент5.D10
  N10: Q17.C, Q18.C
  GND: Компонент5.GND, R3.Pin_1, Компонент6.GND
  N11: Компонент5.D5, Q23.E, Q24.E
  N12: Компонент5.D6, Q21.E, Q22.E
  N13: Компонент5.D7, Компонент6.CS
  N14: Компонент5.D8, Компонент6.CE
  N15: Компонент5.D9, Q19.E, Q20.E
  N16: Компонент5.D11/MOSI, Компонент6.MOSI
  N17: Компонент5.D12/MISO, Компонент6.MISO
  3V3: Компонент5.3V3, Компонент6.VCC
  N18: Компонент5.D13/SCK, Компонент6.SCK
  N19: Q19.C, Q20.C
