# Fritzing sketch receiver_ble (saved by Fritzing 0.9.5d)
breadboards: 1

parts:
  S1 = Round Pushbutton
  M3 = DC Motor
  M4 = DC Motor  # not connected
  LED2 = LED - 5mm [color="Blue (470nm)" package="5 mm [THT]"]
  VCC3 = Battery
  VCC4 = Battery
  Q9 = NPN-Transistor [package="TO92 [THT]"]
  Q10 = PNP-Transistor [package="TO92 [THT]"]
  Компонент3 = Arduino Nano (Rev3.0)
  Q11 = NPN-Transistor [package="TO92 [THT]"]
  Q12 = PNP-Transistor [package="TO92 [THT]"]
  Q13 = NPN-Transistor [package="TO92 [THT]"]
  Q14 = PNP-Transistor [package="TO92 [THT]"]
  Q15 = NPN-Transistor [package="TO92 [THT]"]
  Q16 = PNP-Transistor [package="TO92 [THT]"]
  R2 = Resistor [tolerance=±5% resistance=10000 package=THT]
  Компонент4 = NRF24L01+ Breakout Board

nets:
  N1: S1.leg0, Компонент3.D3
  GND: S1.leg1, Компонент3.GND, R2.Pin_1, Компонент4.GND
  N2: M3.pin_1, Q15.C, Q16.C
  N3: M3.pin_2, Q13.C, Q14.C
  N4: LED2.cathode, Компонент3.D2
  N5: LED2.anode, R2.Pin_0
  N6: VCC3.-, Q10.B, Q12.B
  N7: VCC3.+, Q9.B, Q11.B
  N8: VCC4.-, Q14.B, Q16.B
  N9: VCC4.+, Q13.B, Q15.B
  N10: Q9.E, Q10.E, Компонент3.D10
  N11: Q9.C, Q10.C
  N12: Компонент3.D5, Q15.E, Q16.E
  N13: Компонент3.D6, Q13.E, Q14.E
  N14: Компонент3.D7, Компонент4.CS
  N15: Компонент3.D8, Компонент4.CE
  N16: Компонент3.D9, Q11.E, Q12.E
  N17: Компонент3.D11/MOSI, Компонент4.MOSI
  N18: Компонент3.D12/MISO, Компонент4.MISO
  3V3: Компонент3.3V3, Компонент4.VCC
  N19: Компонент3.D13/SCK, Компонент4.SCK
  N20: Q11.C, Q12.C
