# Fritzing sketch receiver_esp32 (saved by Fritzing 0.9.5d)
breadboards: 1

parts:
  S3 = Round Pushbutton
  M5 = DC Motor
  M6 = DC Motor  # not connected
  LED3 = LED - 5mm [color="Blue (470nm)" package="5 mm [THT]"]
  VCC5 = Battery
  VCC6 = Battery
  S4 = Round Pushbutton
  Q17 = NPN-Transistor [package="TO92 [THT]"]
  Q18 = PNP-Transistor [package="TO92 [THT]"]
  Компонент5 = Arduino Nano (Rev3.0)
  Q19 = NPN-Transistor [package="TO92 [THT]"]
  Q20 = PNP-Transistor [package="TO92 [THT]"]
  Q21 = NPN-Transistor [package="TO92 [THT]"]
  Q22 = PNP-Transistor [package="TO92 [THT]"]
  Q23 = NPN-Transistor [package="TO92 [THT]"]
  Q24 = PNP-Transistor [package="TO92 [THT]"]
  R3 = Resistor [tolerance=±5% resistance=10000 package=THT]
  Компонент6 = NRF24L01+ Breakout Board

nets:
  GND: S3.leg0, S4.leg1, Компонент5.GND, R3.Pin_1, Компонент6.GND
  N1: S3.leg1, Компонент5.A7
  N2: M5.pin_1, Q23.C, Q24.C
  N3: M5.pin_2, Q21.C, Q22.C
  N4: LED3.cathode, Компонент5.D2
  N5: LED3.anode, R3.Pin_0
  N6: VCC5.-, Q18.B, Q20.B
  N7: VCC5.+, Q17.B, Q19.B
  N8: VCC6.-, Q22.B, Q24.B
  N9: VCC6.+, Q21.B, Q23.B
  N10: S4.leg0, Компонент5.D3
  N11: Q17.E, Q18.E, Компонент5.D10
  N12: Q17.C, Q18.C
  N13: Компонент5.D5, Q23.E, Q24.E
  N14: Компонент5.D6, Q21.E, Q22.E
  N15: Компонент5.D7, Компонент6.CS
  N16: Компонент5.D8, Компонент6.CE
  N17: Компонент5.D9, Q19.E, Q20.E
  N18: Компонент5.D11/MOSI, Компонент6.MOSI
  N19: Компонент5.D12/MISO, Компонент6.MISO
  3V3: Компонент5.3V3, Компонент6.VCC
  N20: Компонент5.D13/SCK, Компонент6.SCK
  N21: Q19.C, Q20.C
