# Fritzing sketch transiever (saved by Fritzing 0.9.5d)
breadboards: 1

parts:
  Компонент1 = Arduino Nano (Rev3.0)
  Компонент2 = NRF24L01+ Breakout Board
  Компонент3 = Thumb Joystick

nets:
  GND: Компонент1.GND, Компонент2.GND, Компонент3.GND
  N1: Компонент1.D2, Компонент3.SEL
  N2: Компонент1.D7, Компонент2.CS
  N3: Компонент1.D8, Компонент2.CE
  N4: Компонент1.D11/MOSI, Компонент2.MOSI
  N5: Компонент1.D12/MISO, Компонент2.MISO
  5V: Компонент1.5V, Компонент3.VCC
  N6: Компонент1.A7, Компонент3.HORZ
  N7: Компонент1.A6, Компонент3.VERT
  3V3: Компонент1.3V3, Компонент2.VCC
  N8: Компонент1.D13/SCK, Компонент2.SCK
