# Fritzing sketch tranciever_esp32 (saved by Fritzing 0.9.5d)
breadboards: 1

parts:
  U1 = ESP32S-HiLetgo [part_number=ESP32S-HiLetgo]
  Компонент1 = NRF24L01+ Breakout Board

nets:
  N1: U1.GPIO14, Компонент1.MISO
  N2: U1.GPIO12, Компонент1.SCK
  N3: U1.GND, Компонент1.MOSI
  N4: U1.GPIO13, Компонент1.CS
  N5: U1.GPIO9, Компонент1.CE
  N6: U1.GPIO11, Компонент1.GND
  VIN: U1.VIN, Компонент1.VCC

custom parts:
  ESP32S-HiLetgo: HiLetgo ESP-WROOM-32 ESP32 ESP-32S Development Board 2.4GHz Dual-Mode WiFi + Bluetooth Dual Cores Microcontroller The ESP32 integrated with Antenna switches, RF Balun, power amplifiers, low-noise amplifiers, filters, and management modules, and the entire solution occupies the least area of PCB. 2.4 GHz Wi-Fi plus Bluetooth dual-mode chip, with TSMC Ultra-low power consumption 40nm technology,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
